# Fritzing sketch main-schema (saved by Fritzing 1.0.4)
breadboards: 1

parts:
  BAT2 = BC9VPC [package=bc9vpc]
  A4 = mini560 [package=THT]
  A9 = Esp32-c3 super mini-custom
  R1 = Rotary Potentiometer (Small) [maximum_resistance=10kΩ knob_status=50% power=0.5W package=THT]
  S1 = 0.91 inch OLED I2C Display 128 x 32 Pixels
  S2 = Pushbutton [package="[SMD]"]
  LED1 = smd LED [color="Red (633nm)" package="0603 [SMD]"]
  R4 = Resistor [tolerance=±5% resistance=10k package="0603 [SMD]"]
  R5 = Resistor [tolerance=±5% resistance=220 package="0603 [SMD]"]
  Part1 = Thumb Joystick
  S3 = Pushbutton [package="[SMD]"]
  R6 = Resistor [tolerance=±5% resistance=10k package="0603 [SMD]"]

nets:
  N1: BAT2.V+, A4.pin_1, A4.pin_2
  GND: BAT2.V-, A4.pin_3, A4.pin_4, A4.pin_6, A4.pin_7, A9.Pin_15, R1.leg1, S1.GND, S2.Pin_1, S2.Pin_2, LED1.cathode, Part1.GND, S3.Pin_1, S3.Pin_2
  N2: A4.pin_8, A4.pin_9, A9.Pin_16
  N3: A9.Pin_1, R1.wiper
  N4: A9.Pin_2, S1.SDA
  N5: A9.Pin_3, S1.SCL
  N6: A9.Pin_11, S2.Pin_3, S2.Pin_4, R4.Pin_0
  N7: A9.Pin_12, S3.Pin_3, S3.Pin_4, R6.Pin_0
  N8: A9.Pin_13, R5.Pin_1
  VCC: A9.Pin_14, R1.leg2, S1.VCC, R4.Pin_1, Part1.VCC, R6.Pin_1
  N9: LED1.anode, R5.Pin_0

custom parts:
  mini560: 5A DC-DC Mini 560 Step Down Stabilized Voltage Supply Module Output 3.3 5V 9V 12V Step-down Power Converter Board Module
  Esp32-c3 super mini-custom: ESP32-C3 Development Board ESP32 SuperMini Development Board ESP32 Development Board WiFi Bluetooth.
